# Fritzing sketch прототип 1 (saved by Fritzing 0.9.3b)
breadboards: 1

parts:
  Часть1 = Arduino Uno (Rev3)
  Disp1 = LBT2088AH [part_number=LBT2088AH]
  J1 = Piezo Speaker
  Q1 = NPN-Transistor [package="TO92 [THT]"]
  S1 = Pushbutton [package="[THT]"]
  S2 = Pushbutton [package="[THT]"]
  S3 = Pushbutton [package="[THT]"]
  S4 = Pushbutton [package="[THT]"]
  S5 = Toggle Switch [package=THT]
  VCC1 = Battery

nets:
  N1: Часть1.D2, S1.Pin_3, S1.Pin_4
  N2: Часть1.D3_PWM, S4.Pin_3, S4.Pin_4
  N3: Часть1.D4, S2.Pin_3, S2.Pin_4
  N4: Часть1.D5_PWM, S3.Pin_3, S3.Pin_4
  N5: Часть1.D6_PWM, Disp1.pin_6
  N6: Часть1.D7, Q1.B
  N7: Часть1.GND, Disp1.pin_7, J1.pin1, S1.Pin_1, S1.Pin_2, S2.Pin_1, S2.Pin_2, S3.Pin_1, S3.Pin_2, S4.Pin_1, S4.Pin_2, S5.L2
  N8: Часть1.VIN, Disp1.pin_8, Q1.C, VCC1.+
  N9: J1.pin2, Q1.E
  N10: S5.L1, VCC1.-
